// Logisim project hw3.circ as structural Verilog: 5 circuits, main circuit 16-bit ALU
module _16_bit_Full_Adder (
  input  [15:0] A,
  input  [15:0] B,
  input  Carry_In,
  output [15:0] Answer,
  output Carry_Out
);

  wire n4_bit_full_adder_2_carry_out, n4_bit_full_adder_3_carry_out, n4_bit_full_adder_4_carry_out;

  _4_bit_Full_Adder u_4_bit_full_adder_1 (
    .A(A[15:12]), .Carry_Out(Carry_Out), .Answer(Answer[15:12]), .B(B[15:12]),
    .Carry_In(n4_bit_full_adder_2_carry_out));
  _4_bit_Full_Adder u_4_bit_full_adder_2 (
    .A(A[11:8]), .Carry_Out(n4_bit_full_adder_2_carry_out), .Answer(Answer[11:8]), .B(B[11:8]),
    .Carry_In(n4_bit_full_adder_3_carry_out));
  _4_bit_Full_Adder u_4_bit_full_adder_3 (
    .A(A[7:4]), .Carry_Out(n4_bit_full_adder_3_carry_out), .Answer(Answer[7:4]), .B(B[7:4]),
    .Carry_In(n4_bit_full_adder_4_carry_out));
  _4_bit_Full_Adder u_4_bit_full_adder_4 (
    .A(A[3:0]), .Carry_Out(n4_bit_full_adder_4_carry_out), .Answer(Answer[3:0]), .B(B[3:0]),
    .Carry_In(Carry_In));
endmodule

module _1_bit_Full_Adder (
  input  A,
  input  B,
  input  Carry_In,
  output out_4,
  output out_5
);

  wire and_2_out, and_3_out, and_4_out, and_5_out, and_6_out, and_7_out, and_8_out;

  // AND_Gate and_1 has open pins: in0=A, in1=B, in2=Carry_In, out=open
  and and_2 (and_2_out, ~A, ~B, Carry_In);  // AND_Gate
  and and_3 (and_3_out, ~A, B, ~Carry_In);  // AND_Gate
  and and_4 (and_4_out, ~A, B, Carry_In);  // AND_Gate
  and and_5 (and_5_out, A, ~B, ~Carry_In);  // AND_Gate
  and and_6 (and_6_out, A, ~B, Carry_In);  // AND_Gate
  and and_7 (and_7_out, A, B, ~Carry_In);  // AND_Gate
  and and_8 (and_8_out, A, B, Carry_In);
  or or_1 (out_4, and_4_out, and_6_out, and_7_out, and_8_out);
  or or_2 (out_5, and_8_out, and_2_out, and_3_out, and_5_out);

  // Other names for the same wires on the sheet: Answer = out_5; Carry_Out = out_4
endmodule

module _4_bit_Full_Adder (
  input  [3:0] A,
  input  [3:0] B,
  input  Carry_In,
  output Carry_Out,
  output [3:0] Answer
);

  wire n1_bit_full_adder_2_out_4, n1_bit_full_adder_3_out_4, n1_bit_full_adder_4_out_4;

  _1_bit_Full_Adder u_1_bit_full_adder_1 (
    .A(A[3]), .B(B[3]), .Carry_In(n1_bit_full_adder_2_out_4), .out_4(Carry_Out), .out_5(Answer[3]));
  _1_bit_Full_Adder u_1_bit_full_adder_2 (
    .A(A[2]), .B(B[2]), .Carry_In(n1_bit_full_adder_3_out_4), .out_4(n1_bit_full_adder_2_out_4),
    .out_5(Answer[2]));
  _1_bit_Full_Adder u_1_bit_full_adder_3 (
    .A(A[1]), .B(B[1]), .Carry_In(n1_bit_full_adder_4_out_4), .out_4(n1_bit_full_adder_3_out_4),
    .out_5(Answer[1]));
  _1_bit_Full_Adder u_1_bit_full_adder_4 (
    .A(A[0]), .B(B[0]), .Carry_In(Carry_In), .out_4(n1_bit_full_adder_4_out_4), .out_5(Answer[0]));
endmodule

module _4_bit_ALU (
  input  [3:0] A,
  input  [3:0] B,
  input  S0,
  input  S1,
  input  S2,
  output [3:0] out_6
);

  wire n4_bit_full_adder_3_carry_out, n4_bit_full_adder_4_carry_out;
  wire [3:0] _2_s_Complement, AND, Decrement, Multiply_by_4, n4_bit_full_adder_2_answer,
       n4_bit_full_adder_3_answer, n4_bit_full_adder_4_answer, not_1_out, not_2_out, not_3_out, OR,
       Subtraction, XOR;

  _4_bit_Full_Adder u_4_bit_full_adder_1 (
    .A(A), .Answer(Subtraction), .B(not_1_out), .Carry_In(1'b1));  // open: Carry_Out
  assign XOR = A ^ B;  // XOR_Gate XOR, 4 bits wide
  assign not_1_out = ~B;  // NOT_Gate not_1, 4 bits wide
  _4_bit_Full_Adder u_4_bit_full_adder_2 (
    .A(A), .Answer(n4_bit_full_adder_2_answer), .B(B), .Carry_In(1'b0));  // open: Carry_Out
  _4_bit_Full_Adder u_4_bit_full_adder_3 (
    .A(A), .Carry_Out(n4_bit_full_adder_3_carry_out), .Answer(n4_bit_full_adder_3_answer),
    .B(n4_bit_full_adder_4_answer), .Carry_In(n4_bit_full_adder_4_carry_out));
  _4_bit_Full_Adder u_4_bit_full_adder_4 (
    .A(A), .Carry_Out(n4_bit_full_adder_4_carry_out), .Answer(n4_bit_full_adder_4_answer), .B(A),
    .Carry_In(1'b0));
  _4_bit_Full_Adder u_4_bit_full_adder_5 (
    .A(A), .Answer(Multiply_by_4), .B(n4_bit_full_adder_3_answer), .Carry_In(n4_bit_full_adder_3_carry_out));  // open: Carry_Out
  _4_bit_Full_Adder u_4_bit_full_adder_6 (
    .A(A), .Answer(Decrement), .B(not_2_out), .Carry_In(1'b1));  // open: Carry_Out
  assign not_2_out = ~4'b0001;  // NOT_Gate not_2, 4 bits wide
  assign OR = A | B;  // OR_Gate OR, 4 bits wide
  Multiplexer #(.select(3), .width(4), .disabled(0), .enable("false")) multiplexer_1 (
    .in0(n4_bit_full_adder_2_answer), .in1(Subtraction), .in2(Decrement), .in3(_2_s_Complement),
    .in4(Multiply_by_4), .in5(AND), .in6(OR), .in7(XOR), .out(out_6), .sel({S2, S1, S0}));
  assign not_3_out = ~A;  // NOT_Gate not_3, 4 bits wide
  _4_bit_Full_Adder u_4_bit_full_adder_7 (
    .A(not_3_out), .Answer(_2_s_Complement), .B(4'b0000), .Carry_In(1'b1));  // open: Carry_Out
  assign AND = A & B;  // AND_Gate AND, 4 bits wide

  // Other names for the same wires on the sheet: Answer[3:0] = out_6; Selectors[2:0] = {S2, S1, S0}

  // Notes on the sheet:
  //   Inputs:
  //   000 - Addition
  //   001 - Subtraction
  //   010 - Decrement
  //   100 - Multiply by 4
  //   101 - AND
  //   110 - OR
  //   111 - XOR
  //   011 - 2's Compliment Negation
  //   001 - Subtraction
  //   111 - XOR
  //   000 - Addition
  //   100 - Multiply by 4
  //   010 - Decrement
  //   110 - OR
  //   011 - 2's Compliment Negation
  //   101 - AND
endmodule

module _16_bit_ALU (
  input  [15:0] A,
  input  [15:0] B,
  input  S0,
  input  S1,
  input  S2,
  output [15:0] out_6
);

  wire n16_bit_full_adder_2_carry_out, n16_bit_full_adder_4_carry_out;
  wire [15:0] _2_s_Complement, AND, Decrement, Multiply_by_4, n16_bit_full_adder_2_answer,
       n16_bit_full_adder_3_answer, n16_bit_full_adder_4_answer, not_1_out, not_2_out, not_3_out, OR,
       Subtraction, XOR;

  _16_bit_Full_Adder u_16_bit_full_adder_1 (
    .A(A), .B(not_1_out), .Carry_In(1'b1), .Answer(Subtraction));  // open: Carry_Out
  assign not_1_out = ~B;  // NOT_Gate not_1, 16 bits wide
  assign XOR = A ^ B;  // XOR_Gate XOR, 16 bits wide
  _16_bit_Full_Adder u_16_bit_full_adder_2 (
    .A(A), .B(A), .Carry_In(1'b0), .Answer(n16_bit_full_adder_2_answer),
    .Carry_Out(n16_bit_full_adder_2_carry_out));
  _16_bit_Full_Adder u_16_bit_full_adder_3 (
    .A(A), .B(B), .Carry_In(1'b0), .Answer(n16_bit_full_adder_3_answer));  // open: Carry_Out
  _16_bit_Full_Adder u_16_bit_full_adder_4 (
    .A(A), .B(n16_bit_full_adder_2_answer), .Carry_In(n16_bit_full_adder_2_carry_out),
    .Answer(n16_bit_full_adder_4_answer), .Carry_Out(n16_bit_full_adder_4_carry_out));
  _16_bit_Full_Adder u_16_bit_full_adder_5 (
    .A(A), .B(not_2_out), .Carry_In(1'b1), .Answer(Decrement));  // open: Carry_Out
  assign OR = A | B;  // OR_Gate OR, 16 bits wide
  _16_bit_Full_Adder u_16_bit_full_adder_6 (
    .A(A), .B(n16_bit_full_adder_4_answer), .Carry_In(n16_bit_full_adder_4_carry_out), .Answer(Multiply_by_4));  // open: Carry_Out
  assign not_2_out = ~16'h1;  // NOT_Gate not_2, 16 bits wide
  Multiplexer #(.select(3), .width(16), .disabled(0), .enable("false")) multiplexer_1 (
    .in0(n16_bit_full_adder_3_answer), .in1(Subtraction), .in2(Decrement), .in3(_2_s_Complement),
    .in4(Multiply_by_4), .in5(AND), .in6(OR), .in7(XOR), .out(out_6), .sel({S2, S1, S0}));
  assign not_3_out = ~A;  // NOT_Gate not_3, 16 bits wide
  _16_bit_Full_Adder u_16_bit_full_adder_7 (
    .A(not_3_out), .B({16{1'b0}}), .Carry_In(1'b1), .Answer(_2_s_Complement));  // open: Carry_Out
  assign AND = A & B;  // AND_Gate AND, 16 bits wide

  // Other names for the same wires on the sheet: Answer[15:0] = out_6; Selectors[2:0] = {S2, S1, S0}

  // Notes on the sheet:
  //   000 - Addition
  //   001 - Subtraction
  //   010 - Decrement
  //   100 - Multiply by 4
  //   101 - AND
  //   110 - OR
  //   111 - XOR
  //   011 - 2's Compliment Negation
  //   001 - Subtraction
  //   111 - XOR
  //   000 - Addition
  //   100 - Multiply by 4
  //   010 - Decrement
  //   110 - OR
  //   011 - 2's Compliment Negation
  //   101 - AND
endmodule
