// Logisim project hw4part1.circ as structural Verilog: 2 circuits, main circuit One Hot State Machine
module One_Hot_State_Machine (
  input  G,
  input  Clock,
  input  Reset,
  output W,
  output X,
  output Y,
  output Z
);

  wire and_1_out, and_2_out, and_3_out, and_4_out, and_5_out, and_6_out, and_7_out, and_10_out, and_11_out,
       N0, N1, N2, N3, N4, N5, N6, S0, S1, S2, S3, S4, S5, S6;

  and and_1 (and_1_out, S0, ~G);  // AND_Gate
  and and_2 (and_2_out, S6, ~G);  // AND_Gate
  and and_3 (and_3_out, S0, G);
  and and_4 (and_4_out, S3, ~G);  // AND_Gate
  and and_5 (and_5_out, S1, G);
  and and_6 (and_6_out, S4, ~G);  // AND_Gate
  and and_7 (and_7_out, S1, ~G);  // AND_Gate
  and and_8 (N4, S3, G);
  and and_9 (N5, S4, G);
  and and_10 (and_10_out, S6, G);
  Register #(.width(7)) register_1 (
    .D({N6, N5, N4, N3, N2, N1, N0}), .en(1'b1), .Q({S6, S5, S4, S3, S2, S1, S0}), .clk(Clock), .clr(Reset));
  and and_11 (and_11_out, ~S0, ~S1, ~S2, ~S3, ~S4, ~S5, ~S6);  // AND_Gate
  or or_1 (N0, and_11_out, and_1_out, and_2_out);
  or or_2 (N1, and_3_out, and_4_out);
  or or_3 (N2, and_5_out, and_6_out);
  or or_4 (N3, and_7_out, S2);
  or or_5 (N6, and_10_out, S5);
  or or_6 (W, S0, S3, S5);
  or or_7 (X, S3, S6);
  or or_8 (Y, S3, S2, S4, S5);
  or or_9 (Z, S4, S6);

  // Other names for the same wires on the sheet: CLK = Clock; RST = Reset

  // Notes on the sheet:
  //   My name is:
  //   Mani Japra
  //   and this is my one-hot machine
  //   State 0
  //   State 1
  //   State 2
  //   State 3
  //   State 4
  //   State 5
  //   State 6
  //   Outputs:
endmodule

module Tester (
  input  G
);

  wire CLK_out, one_hot_state_machine_1_w, one_hot_state_machine_1_x, one_hot_state_machine_1_y,
       one_hot_state_machine_1_z, RST_out;

  Clock CLK (.out(CLK_out));
  One_Hot_State_Machine one_hot_state_machine_1 (
    .G(G), .Clock(CLK_out), .Reset(RST_out), .W(one_hot_state_machine_1_w), .X(one_hot_state_machine_1_x),
    .Y(one_hot_state_machine_1_y), .Z(one_hot_state_machine_1_z));
  LED led_1 (.in(one_hot_state_machine_1_w));
  LED led_2 (.in(one_hot_state_machine_1_x));
  LED led_3 (.in(one_hot_state_machine_1_y));
  LED led_4 (.in(one_hot_state_machine_1_z));
  Button RST (.out(RST_out));
endmodule
