// Logisim project Japra_Maninder.circ as structural Verilog: 7 circuits, main circuit main
module main (
);

  wire A_MUX_0, A_MUX_1, A_MUX_2, A_MUX_3, ALU_PC_Sel, and_1_out, and_2_out, and_6_out, B_MUX_0, B_MUX_1,
       B_MUX_2, B_MUX_3, B_Select, Clock, comparator_1_eq, comparator_2_eq, comparator_4_eq, comparator_5_eq,
       comparator_6_eq, comparator_7_eq, comparator_9_eq, comparator_10_eq, comparator_11_eq, FlushA, FlushB,
       IF_IDRR_Stall_Check, isLW_MEM, isSW_MEM, isSW_OR_BEQ, or_3_out, or_5_out, PC_Enable, Stall, TakeB,
       WrEn;
  wire [0:0] PC_Select;
  wire [1:0] A_MUX, ALU_Func, B_MUX;
  wire [3:0] bitselector_1_out, bitselector_2_out, bitselector_3_out, bitselector_5_out, Execute_RX, MEM_RX,
       RX, RY, RZ, WB_RX;
  wire [6:0] MEM_ControlSig;
  wire [8:0] ID_ControlSig, MEM_WB_Buffer_controlsig_out;
  wire [8:3] Execute_ControlSig;
  wire [19:0] ID_Immediate, IDRR_EX_Buffer_imm_out;
  wire [31:0] A, alu_1_out, ALU_OUT, ALU_PC, B, Execute_A, Execute_B, Execute_Imm, Execute_PC, ID_PC,
       IF_IDRR_Buffer_instruction_out, MEM_A, MEM_A_OUT, MEM_B, MEM_IN_OUT, MEM_OUT, multiplexer_9_out, OUT1,
       OUT2, PC___1, PC___Imm, PC_Reg_IN, PC_Reg_OUT, ram_1_data, Result;

  Clock clock_1 (.out(Clock));
  Register #(.width(32)) PC (.D(PC_Reg_IN), .en(PC_Enable), .Q(PC_Reg_OUT), .clk(Clock));  // open: clr
  Adder #(.width(32)) adder_1 (.a(PC_Reg_OUT), .b(32'h1), .out(PC___1));  // open: cin, cout
  Multiplexer #(.select(2), .width(32), .enable("false")) multiplexer_1 (
    .in0(PC___1), .in1(PC___Imm), .in2(Execute_A), .out(PC_Reg_IN),
    .sel({Execute_ControlSig[6], PC_Select[0]}));  // open: in3
  and and_1 (and_1_out, ~Stall, ~ID_ControlSig[4]);  // AND_Gate
  or or_1 (IF_IDRR_Stall_Check, Stall, ID_ControlSig[4]);
  Comparator #(.width(4)) comparator_1 (.a(RY), .b(Execute_RX), .eq(comparator_1_eq));  // open: gt, lt
  Comparator #(.width(4)) comparator_2 (.a(RZ), .b(Execute_RX), .eq(comparator_2_eq));  // open: gt, lt
  and and_2 (and_2_out, Execute_ControlSig[5], TakeB);
  Comparator #(.width(4)) comparator_3 (.a(RY), .b(4'b0000), .eq(A_MUX_0));  // open: gt, lt
  Comparator #(.width(4)) comparator_4 (.a(RY), .b(RX), .eq(comparator_4_eq));  // open: gt, lt
  Comparator #(.width(4)) comparator_5 (.a(RY), .b(Execute_RX), .eq(comparator_5_eq));  // open: gt, lt
  Comparator #(.width(4)) comparator_6 (.a(RY), .b(MEM_RX), .eq(comparator_6_eq));  // open: gt, lt
  Comparator #(.width(4)) comparator_7 (.a(RY), .b(WB_RX), .eq(comparator_7_eq));  // open: gt, lt
  Multiplexer #(.width(32), .enable("false")) multiplexer_2 (
    .in0(ALU_OUT), .in1(ID_PC), .out(ALU_PC), .sel(ALU_PC_Sel));
  Multiplexer #(.width(32), .enable("false")) multiplexer_3 (
    .in0(MEM_A), .in1(MEM_OUT), .out(MEM_IN_OUT), .sel(isLW_MEM));
  Comparator #(.width(4)) comparator_8 (.a(RZ), .b(4'b0000), .eq(B_MUX_0));  // open: gt, lt
  Comparator #(.width(4)) comparator_9 (.a(RZ), .b(Execute_RX), .eq(comparator_9_eq));  // open: gt, lt
  Comparator #(.width(4)) comparator_10 (.a(RZ), .b(MEM_RX), .eq(comparator_10_eq));  // open: gt, lt
  Comparator #(.width(4)) comparator_11 (.a(RZ), .b(WB_RX), .eq(comparator_11_eq));  // open: gt, lt
  RAM #(.addrWidth(24), .dataWidth(32)) ram_1 (
    .addr(PC_Reg_OUT[23:0]), .data(ram_1_data), .clk(Clock));  // open: sel, ld, clr
  or or_2 (PC_Enable, and_1_out, FlushA, Execute_ControlSig[6]);
  or or_3 (or_3_out, comparator_1_eq, comparator_2_eq);
  or or_4 (FlushA, Execute_ControlSig[6], and_2_out);
  or or_5 (or_5_out, Execute_ControlSig[6], and_2_out);
  Dual_Ported_Register_File dual_ported_register_file_1 (
    .CLK(Clock), .WrREGNO(WB_RX), .RdREGNO1(RY), .RdREGNO2(RZ), .INPUT(Result), .OUT1(OUT1), .OUT2(OUT2),
    .WrEN(WrEn));
  and and_3 (PC_Select[0], Execute_ControlSig[5], TakeB);
  and and_4 (Stall, Execute_ControlSig[8], or_3_out);
  and and_5 (ALU_PC_Sel, comparator_4_eq, ID_ControlSig[6]);
  or or_6 (A_MUX_1, ALU_PC_Sel, and_6_out);
  and and_6 (and_6_out, comparator_5_eq, Execute_ControlSig[3]);
  and and_7 (A_MUX_2, comparator_6_eq, MEM_ControlSig[3]);
  and and_8 (A_MUX_3, comparator_7_eq, WrEn);
  and and_9 (B_MUX_1, comparator_9_eq, Execute_ControlSig[3]);
  and and_10 (B_MUX_2, comparator_10_eq, MEM_ControlSig[3]);
  and and_11 (B_MUX_3, comparator_11_eq, WrEn);
  or or_7 (FlushB, Stall, or_5_out);
  IF_IDRR_Buffer IF_IDRR_Buffer (
    .Instruction_IN(ram_1_data), .PC_IN(PC___1), .Clock(Clock), .Flush(FlushA), .Stall(IF_IDRR_Stall_Check),
    .Instruction_OUT(IF_IDRR_Buffer_instruction_out), .PC_OUT(ID_PC));
  BitSelector #(.width(32), .group(4)) bitselector_1 (
    .in(IF_IDRR_Buffer_instruction_out), .out(bitselector_1_out), .sel(3'b110));
  BitSelector #(.width(32), .group(4)) bitselector_2 (
    .in(IF_IDRR_Buffer_instruction_out), .out(bitselector_2_out), .sel(3'b101));
  BitSelector #(.width(32), .group(4)) bitselector_3 (
    .in(IF_IDRR_Buffer_instruction_out), .out(bitselector_3_out), .sel(3'b000));
  BitSelector #(.width(32), .group(20)) bitselector_4 (
    .in(IF_IDRR_Buffer_instruction_out), .out(ID_Immediate), .sel(1'b0));
  BitSelector #(.width(32), .group(4)) bitselector_5 (
    .in(IF_IDRR_Buffer_instruction_out), .out(bitselector_5_out), .sel(3'b111));
  or or_8 (isSW_OR_BEQ, ID_ControlSig[7], ID_ControlSig[5]);
  BitFinder #(.width(4)) bitfinder_1 (.in({A_MUX_3, A_MUX_2, A_MUX_1, A_MUX_0}), .index(A_MUX));  // open: found
  Multiplexer #(.select(2), .width(32), .enable("false")) multiplexer_4 (
    .in0(OUT1), .in1(ALU_PC), .in2(MEM_IN_OUT), .in3(Result), .out(A), .sel(A_MUX));
  Multiplexer #(.select(2), .width(32), .enable("false")) multiplexer_5 (
    .in0(OUT2), .in1(ALU_OUT), .in2(MEM_IN_OUT), .in3(Result), .out(B), .sel(B_MUX));
  BitFinder #(.width(4)) bitfinder_2 (.in({B_MUX_3, B_MUX_2, B_MUX_1, B_MUX_0}), .index(B_MUX));  // open: found
  Multiplexer #(.width(4), .enable("false")) multiplexer_6 (
    .in0(bitselector_1_out), .in1(bitselector_2_out), .out(RX), .sel(ID_ControlSig[6]));
  Multiplexer #(.width(4), .enable("false")) multiplexer_7 (
    .in0(bitselector_2_out), .in1(bitselector_1_out), .out(RY), .sel(ID_ControlSig[6]));
  Multiplexer #(.width(4), .enable("false")) multiplexer_8 (
    .in0(bitselector_3_out), .in1(bitselector_1_out), .out(RZ), .sel(isSW_OR_BEQ));
  ROM #(.addrWidth(4), .dataWidth(9)) rom_1 (.addr(bitselector_5_out), .data(ID_ControlSig));  // open: sel
  IDRR_EX_Buffer IDRR_EX_Buffer (
    .RX_IN(RX), .A_IN(A), .B_IN(B), .PC_IN(ID_PC), .Immediate_IN(ID_Immediate),
    .ControlSig_IN(ID_ControlSig), .Clock(Clock), .Flush(FlushB), .Stall(1'b0), .RX_OUT(Execute_RX),
    .A_OUT(Execute_A), .B_OUT(Execute_B), .PC_OUT(Execute_PC), .Imm_OUT(IDRR_EX_Buffer_imm_out),
    .ControlSig_OUT({Execute_ControlSig, B_Select, ALU_Func}));
  assign Execute_Imm = {{12{1'b0}}, IDRR_EX_Buffer_imm_out};  // Bit_Extender bit_extender_1
  Multiplexer #(.width(32), .enable("false")) multiplexer_9 (
    .in0(Execute_B), .in1(Execute_Imm), .out(multiplexer_9_out), .sel(B_Select));
  Adder #(.width(32)) adder_2 (.a(Execute_PC), .b(Execute_Imm), .out(PC___Imm));  // open: cin, cout
  ALU alu_1 (.FUNC(ALU_Func), .A(Execute_A), .B(multiplexer_9_out), .OUT(alu_1_out));
  Comparator #(.width(32)) comparator_12 (.a({32{1'b0}}), .b(alu_1_out), .eq(TakeB));  // open: gt, lt
  Multiplexer #(.width(32), .enable("false")) multiplexer_10 (
    .in0(alu_1_out), .in1(Execute_PC), .out(ALU_OUT), .sel(Execute_ControlSig[6]));
  EX_MEM_Buffer EX_MEM_Buffer (
    .RX_IN(Execute_RX), .A_IN(ALU_OUT), .B_IN(Execute_B),
    .ControlSig_IN({Execute_ControlSig, B_Select, ALU_Func}), .Clock(Clock), .RX_OUT(MEM_RX), .A_OUT(MEM_A),
    .B_OUT(MEM_B),
    .ControlSig_OUT({isLW_MEM, isSW_MEM, MEM_ControlSig[6], ID_ControlSig[5], MEM_ControlSig[4:0]}));
  Multiplexer #(.width(32), .enable("false")) multiplexer_11 (
    .in0(MEM_A), .in1(MEM_OUT), .out(MEM_A_OUT), .sel(isLW_MEM));
  RAM #(.addrWidth(24), .dataWidth(32), .bus("separate")) ram_2 (
    .addr(MEM_A[23:0]), .din(MEM_B), .data(MEM_OUT), .str(isSW_MEM), .clk(Clock), .ld(isLW_MEM));  // open: sel, clr
  MEM_WB_Buffer MEM_WB_Buffer (
    .RX_IN(MEM_RX), .A_IN(MEM_A_OUT),
    .ControlSig_IN({isLW_MEM, isSW_MEM, MEM_ControlSig[6], ID_ControlSig[5], MEM_ControlSig[4:0]}),
    .Clock(Clock), .RX_OUT(WB_RX), .A_OUT(Result),
    .ControlSig_OUT({MEM_WB_Buffer_controlsig_out[8:4], WrEn, MEM_WB_Buffer_controlsig_out[2:0]}));

  // Other names for the same wires on the sheet: Execute_ControlSig[2:0] = {B_Select, ALU_Func};
  //   WrEn_Execute = Execute_ControlSig[3]; isBEQ_Execute = Execute_ControlSig[5];
  //   isJALR_Execute = Execute_ControlSig[6]; PC_Select[1] = Execute_ControlSig[6];
  //   isLW_Execute = Execute_ControlSig[8]; OPCode_4 = ID_ControlSig[4]; isJALR = ID_ControlSig[6];
  //   isSW = ID_ControlSig[7]; WrEn_MEM = MEM_ControlSig[3]; isBEQ = ID_ControlSig[5];
  //   MEM_ControlSig (some bits) = {isLW_MEM, isSW_MEM, ID_ControlSig[5]}; WrRegNo[3:0] = WB_RX

  // Notes on the sheet:
  //   Main Pipeline
  //   Forwarding/Flushing/Stalling
  //   Mani Japra
  //   902958199
  //   contents of rom_1 (hex, n*v repeats v):
  //   8 9 c 10c 84 22 48 10
endmodule

module Dual_Ported_Register_File (
  input  CLK,
  input  WrEN,
  input  [3:0] WrREGNO,
  input  [3:0] RdREGNO1,
  input  [3:0] RdREGNO2,
  input  [31:0] INPUT,
  output [31:0] OUT1,
  output [31:0] OUT2
);

  wire En_a0, En_a1, En_a2, En_a3, En_a4, En_at, En_fp, En_k0, En_ra, En_s0, En_s1, En_s2, En_s3, En_sp,
       En_v0;
  wire [31:0] a0, a1, a2, a3, a4, at, fp, k0, ra, s0, s1, s2, s3, sp, v0, zero;

  Decoder #(.select(4), .disabled(0)) decoder_1 (
    .out1(En_at), .out2(En_v0), .out3(En_a0), .out4(En_a1), .out5(En_a2), .out6(En_a3), .out7(En_a4),
    .out8(En_s0), .out9(En_s1), .out10(En_s2), .out11(En_s3), .out12(En_k0), .out13(En_sp), .out14(En_fp),
    .out15(En_ra), .sel(WrREGNO), .en(WrEN));  // open: out0
  Register #(.width(32)) u_zero (.D(INPUT), .en(1'b0), .Q(zero), .clk(CLK));  // open: clr
  Register #(.width(32)) u_at (.D(INPUT), .en(En_at), .Q(at), .clk(CLK));  // open: clr
  Register #(.width(32)) u_v0 (.D(INPUT), .en(En_v0), .Q(v0), .clk(CLK));  // open: clr
  Register #(.width(32)) u_a0 (.D(INPUT), .en(En_a0), .Q(a0), .clk(CLK));  // open: clr
  Register #(.width(32)) u_a1 (.D(INPUT), .en(En_a1), .Q(a1), .clk(CLK));  // open: clr
  Register #(.width(32)) u_a2 (.D(INPUT), .en(En_a2), .Q(a2), .clk(CLK));  // open: clr
  Register #(.width(32)) u_a3 (.D(INPUT), .en(En_a3), .Q(a3), .clk(CLK));  // open: clr
  Register #(.width(32)) u_a4 (.D(INPUT), .en(En_a4), .Q(a4), .clk(CLK));  // open: clr
  Multiplexer #(.select(4), .width(32), .disabled(0), .enable("false")) multiplexer_1 (
    .in0(zero), .in1(at), .in2(v0), .in3(a0), .in4(a1), .in5(a2), .in6(a3), .in7(a4), .in8(s0), .in9(s1),
    .in10(s2), .in11(s3), .in12(k0), .in13(sp), .in14(fp), .in15(ra), .out(OUT2), .sel(RdREGNO2));
  Register #(.width(32)) u_s0 (.D(INPUT), .en(En_s0), .Q(s0), .clk(CLK));  // open: clr
  Register #(.width(32)) u_s1 (.D(INPUT), .en(En_s1), .Q(s1), .clk(CLK));  // open: clr
  Register #(.width(32)) u_s2 (.D(INPUT), .en(En_s2), .Q(s2), .clk(CLK));  // open: clr
  Register #(.width(32)) u_s3 (.D(INPUT), .en(En_s3), .Q(s3), .clk(CLK));  // open: clr
  Register #(.width(32)) u_k0 (.D(INPUT), .en(En_k0), .Q(k0), .clk(CLK));  // open: clr
  Register #(.width(32)) u_sp (.D(INPUT), .en(En_sp), .Q(sp), .clk(CLK));  // open: clr
  Register #(.width(32)) u_fp (.D(INPUT), .en(En_fp), .Q(fp), .clk(CLK));  // open: clr
  Register #(.width(32)) u_ra (.D(INPUT), .en(En_ra), .Q(ra), .clk(CLK));  // open: clr
  Multiplexer #(.select(4), .width(32), .disabled(0), .enable("false")) multiplexer_2 (
    .in0(zero), .in1(at), .in2(v0), .in3(a0), .in4(a1), .in5(a2), .in6(a3), .in7(a4), .in8(s0), .in9(s1),
    .in10(s2), .in11(s3), .in12(k0), .in13(sp), .in14(fp), .in15(ra), .out(OUT1), .sel(RdREGNO1));

  // Notes on the sheet:
  //   MODIFY AT YOUR OWN RISK
endmodule

module IF_IDRR_Buffer (
  input  [31:0] Instruction_IN,
  input  [31:0] PC_IN,
  input  Clock,
  input  Flush,
  input  Stall,
  output [31:0] Instruction_OUT,
  output [31:0] PC_OUT
);

  wire Enable;
  wire [31:0] multiplexer_1_out, multiplexer_2_out;

  Multiplexer #(.width(32), .enable("false")) multiplexer_1 (
    .in0(Instruction_IN), .in1({32{1'b0}}), .out(multiplexer_1_out), .sel(Flush));
  Multiplexer #(.width(32), .enable("false")) multiplexer_2 (
    .in0(PC_IN), .in1({32{1'b0}}), .out(multiplexer_2_out), .sel(Flush));
  Register #(.width(32)) register_1 (
    .D(multiplexer_1_out), .en(Enable), .Q(Instruction_OUT), .clk(Clock));  // open: clr
  Register #(.width(32)) register_2 (.D(multiplexer_2_out), .en(Enable), .Q(PC_OUT), .clk(Clock));  // open: clr
  nand nand_1 (Enable, ~Flush, Stall);  // NAND_Gate
endmodule

module IDRR_EX_Buffer (
  input  [3:0] RX_IN,
  input  [31:0] A_IN,
  input  [31:0] B_IN,
  input  [31:0] PC_IN,
  input  [19:0] Immediate_IN,
  input  [8:0] ControlSig_IN,
  input  Clock,
  input  Flush,
  input  Stall,
  output [3:0] RX_OUT,
  output [31:0] A_OUT,
  output [31:0] B_OUT,
  output [31:0] PC_OUT,
  output [19:0] Imm_OUT,
  output [8:0] ControlSig_OUT
);

  wire Enable;
  wire [3:0] multiplexer_1_out;
  wire [8:0] multiplexer_6_out;
  wire [19:0] multiplexer_5_out;
  wire [31:0] multiplexer_2_out, multiplexer_3_out, multiplexer_4_out;

  Multiplexer #(.width(4), .enable("false")) multiplexer_1 (
    .in0(RX_IN), .in1(4'b0000), .out(multiplexer_1_out), .sel(Flush));
  Multiplexer #(.width(32), .enable("false")) multiplexer_2 (
    .in0(A_IN), .in1({32{1'b0}}), .out(multiplexer_2_out), .sel(Flush));
  Multiplexer #(.width(32), .enable("false")) multiplexer_3 (
    .in0(B_IN), .in1({32{1'b0}}), .out(multiplexer_3_out), .sel(Flush));
  Multiplexer #(.width(32), .enable("false")) multiplexer_4 (
    .in0(PC_IN), .in1({32{1'b0}}), .out(multiplexer_4_out), .sel(Flush));
  Multiplexer #(.width(20), .enable("false")) multiplexer_5 (
    .in0(Immediate_IN), .in1({20{1'b0}}), .out(multiplexer_5_out), .sel(Flush));
  Multiplexer #(.width(9), .enable("false")) multiplexer_6 (
    .in0(ControlSig_IN), .in1({9{1'b0}}), .out(multiplexer_6_out), .sel(Flush));
  nand nand_1 (Enable, ~Flush, Stall);  // NAND_Gate
  Register #(.width(4)) register_1 (.D(multiplexer_1_out), .en(Enable), .Q(RX_OUT), .clk(Clock));  // open: clr
  Register #(.width(32)) register_2 (.D(multiplexer_2_out), .en(Enable), .Q(A_OUT), .clk(Clock));  // open: clr
  Register #(.width(32)) register_3 (.D(multiplexer_3_out), .en(Enable), .Q(B_OUT), .clk(Clock));  // open: clr
  Register #(.width(32)) register_4 (.D(multiplexer_4_out), .en(Enable), .Q(PC_OUT), .clk(Clock));  // open: clr
  Register #(.width(20)) register_5 (.D(multiplexer_5_out), .en(Enable), .Q(Imm_OUT), .clk(Clock));  // open: clr
  Register #(.width(9)) register_6 (.D(multiplexer_6_out), .en(Enable), .Q(ControlSig_OUT), .clk(Clock));  // open: clr
endmodule

module EX_MEM_Buffer (
  input  [3:0] RX_IN,
  input  [31:0] A_IN,
  input  [31:0] B_IN,
  input  [8:0] ControlSig_IN,
  input  Clock,
  output [3:0] RX_OUT,
  output [31:0] A_OUT,
  output [31:0] B_OUT,
  output [8:0] ControlSig_OUT
);

  Register #(.width(4)) register_1 (.D(RX_IN), .Q(RX_OUT), .clk(Clock));  // open: en, clr
  Register #(.width(32)) register_2 (.D(A_IN), .Q(A_OUT), .clk(Clock));  // open: en, clr
  Register #(.width(32)) register_3 (.D(B_IN), .Q(B_OUT), .clk(Clock));  // open: en, clr
  Register #(.width(9)) register_4 (.D(ControlSig_IN), .Q(ControlSig_OUT), .clk(Clock));  // open: en, clr
endmodule

module MEM_WB_Buffer (
  input  [3:0] RX_IN,
  input  [31:0] A_IN,
  input  [8:0] ControlSig_IN,
  input  Clock,
  output [3:0] RX_OUT,
  output [31:0] A_OUT,
  output [8:0] ControlSig_OUT
);

  Register #(.width(4)) register_1 (.D(RX_IN), .Q(RX_OUT), .clk(Clock));  // open: en, clr
  Register #(.width(32)) register_2 (.D(A_IN), .Q(A_OUT), .clk(Clock));  // open: en, clr
  Register #(.width(9)) register_3 (.D(ControlSig_IN), .Q(ControlSig_OUT), .clk(Clock));  // open: en, clr
endmodule

module ALU (
  input  [1:0] FUNC,
  input  [31:0] A,
  input  [31:0] B,
  output [31:0] OUT
);

  wire [31:0] adder_1_out, adder_2_out, nand_1_out, subtractor_1_out;

  Adder #(.width(32)) adder_1 (.a(A), .b(B), .out(adder_1_out), .cin(1'b0));  // open: cout
  assign nand_1_out = ~(A & B);  // NAND_Gate nand_1, 32 bits wide
  Subtractor #(.width(32)) subtractor_1 (.a(A), .b(B), .out(subtractor_1_out), .bin(1'b0));  // open: bout
  Adder #(.width(32)) adder_2 (.a(A), .b({32{1'b0}}), .out(adder_2_out), .cin(1'b1));  // open: cout
  Multiplexer #(.select(2), .width(32), .disabled(0), .enable("false")) multiplexer_1 (
    .in0(adder_1_out), .in1(nand_1_out), .in2(subtractor_1_out), .in3(adder_2_out), .out(OUT), .sel(FUNC));

  // Notes on the sheet:
  //   MODIFY AT YOUR OWN RISK
endmodule
