// Logisim project japra_maninder_old.circ as structural Verilog: 7 circuits, main circuit main
module main (
  input  in_1
);

  wire and_1_out, and_2_out, and_3_out, Branch_Enable, BRANCH_NT, Branch_NT_t, Clear, Clock, comparator_1_eq,
       comparator_2_eq, comparator_3_eq, comparator_4_eq, comparator_5_eq, LdPC, not_1_out, or_1_out,
       or_2_out, PC_2_q, Stall, WrEN;
  wire [1:0] WBSelect;
  wire [2:0] adder_3_out, PC_3_q;
  wire [3:0] OPCODE, PC_OPCODE, WrRegNO, WrRegNO2, X, Y, Z;
  wire [19:4] ram_2_data;
  wire [27:0] OUT1;
  wire [31:0] alu_1_out, Branch, Control_Signal, Control_Signal_2, Control_Signal_3, Data_Out, DPRF_OUT1,
       DPRF_OUT2, EX_MEM_IN_1, Immediate_Out, immediate_Out_t, Input, MEM_Data, MEM_Location, MEM_WB_out_13,
       MEM_WB_out_14, MEM_WB_out_15, MEM_WB_pc_out, multiplexer_2_out, OUT2, Out2_t, OUT3, Out3_t, PC,
       PC___1, PC_ADDRESS, PCOUT1, PCOUT2, PCOUT3, RX_value, RX_Value_Out;

  Button button_1 (.out(Clear));
  Clock clock_1 (.out(Clock));
  Multiplexer #(.width(4), .disabled(0), .enable("false")) multiplexer_1 (
    .in0(OUT1[3:0]), .in1(OUT1[23:20]), .out(WrRegNO2), .sel(Control_Signal[2]));
  Register #(.width(32)) u_PC (.D(PC_ADDRESS), .en(LdPC), .Q(PC), .clk(Clock), .clr(Clear));
  Adder #(.width(32)) adder_1 (.a(32'h1), .b(PC), .out(PC___1));  // open: cin, cout
  Multiplexer #(.width(32), .disabled(0), .enable("false")) multiplexer_2 (
    .in0(OUT3), .in1(immediate_Out_t), .out(multiplexer_2_out), .sel(Control_Signal_2[6]));
  Multiplexer #(.select(2), .width(32), .disabled(0), .enable("false")) multiplexer_3 (
    .in0(PC___1), .in1(Branch), .in2(RX_value), .out(PC_ADDRESS), .sel(Control_Signal_2[1:0]));  // open: in3
  ALU alu_1 (.FUNC(Control_Signal_2[5:4]), .A(OUT2), .B(multiplexer_2_out), .OUT(alu_1_out));
  RAM #(.addrWidth(24), .dataWidth(32), .bus("separate")) ram_1 (
    .addr(MEM_Location[23:0]), .din(MEM_Data), .data(Data_Out), .str(Control_Signal_3[8]), .clk(Clock),
    .clr(Clear));  // open: sel, ld
  Dual_Ported_Register_File dual_ported_register_file_1 (
    .CLK(Clock), .WrREGNO(WrRegNO), .RdREGNO1(OUT1[27:24]), .RdREGNO2(WrRegNO2), .INPUT(Input),
    .OUT1(DPRF_OUT1), .OUT2(DPRF_OUT2), .WrEN(WrEN));
  RAM #(.addrWidth(24), .dataWidth(32), .bus("separate")) ram_2 (
    .addr(PC[23:0]), .data({PC_OPCODE, Y, X, ram_2_data, Z}), .ld(1'b1));  // open: din, str, sel, clk, clr
  ROM #(.addrWidth(4), .dataWidth(32)) rom_1 (.addr(OPCODE), .data(Control_Signal));  // open: sel
  Multiplexer #(.width(4), .disabled(0), .enable("false")) multiplexer_4 (
    .in0(OUT1[23:20]), .in1(OUT1[27:24]), .out(WrRegNO), .sel(Control_Signal[11]));
  Adder #(.width(32)) adder_2 (.a(PCOUT2), .b(immediate_Out_t), .out(Branch));  // open: cin, cout
  Comparator #(.width(32), .mode("unsigned")) comparator_1 (
    .a(alu_1_out), .b({32{1'b0}}), .gt(Branch_NT_t), .eq(comparator_1_eq));  // open: lt
  IF_IDRR_Buffer IF_IDRR (
    .Enable(in_1), .Clock(Clock), .Clear(Clear), .PC_IN(PC___1), .in_6({PC_OPCODE, Y, X, ram_2_data, Z}),
    .PC_OUT(PCOUT1), .out_15({OPCODE, OUT1}));  // open: in_2, in_3, in_4, in_5, out_11, out_12, out_13, out_14
  Multiplexer #(.width(32), .disabled(0), .enable("false")) multiplexer_5 (
    .in0(alu_1_out), .in1(Branch), .out(EX_MEM_IN_1), .sel(and_1_out));
  and and_1 (and_1_out, comparator_1_eq, Branch_Enable);
  Comparator #(.width(4), .mode("unsigned")) comparator_2 (
    .a(OUT1[23:20]), .b(Z), .eq(comparator_2_eq));  // open: gt, lt
  Comparator #(.width(32), .mode("unsigned")) comparator_3 (
    .a(PC), .b({32{1'b0}}), .eq(comparator_3_eq));  // open: gt, lt
  Comparator #(.width(4), .mode("unsigned")) comparator_4 (
    .a(OUT1[23:20]), .b(Y), .eq(comparator_4_eq));  // open: gt, lt
  and and_2 (and_2_out, comparator_2_eq, ~comparator_3_eq);  // AND_Gate
  and and_3 (and_3_out, ~comparator_3_eq, comparator_4_eq);  // AND_Gate
  Comparator #(.width(4), .mode("unsigned")) comparator_5 (
    .a(PC_OPCODE), .b(4'b0101), .eq(comparator_5_eq));  // open: gt, lt
  IDRR_EX_Buffer IDRR_EX (
    .Enable(in_1), .Clock(Clock), .Clear(Clear), .PC_IN(PCOUT1), .in_2({{12{1'b0}}, OUT1[19:0]}),
    .in_3(DPRF_OUT2), .in_4(DPRF_OUT2), .in_5(DPRF_OUT1), .in_6(Control_Signal), .PC_OUT(PCOUT2),
    .out_11(Immediate_Out), .out_12(RX_Value_Out), .out_13(Out3_t), .out_14(Out2_t),
    .out_15({Control_Signal_2[31:8], Branch_Enable, Control_Signal_2[6:0]}));
  EX_MEM_Buffer EX_MEM (
    .Enable(in_1), .Clock(Clock), .Clear(Clear), .PC_IN(PCOUT2), .in_3(RX_Value_Out), .in_4(EX_MEM_IN_1),
    .in_6({Control_Signal_2[31:8], Branch_Enable, Control_Signal_2[6:0]}), .PC_OUT(PCOUT3),
    .out_12(MEM_Data), .out_13(MEM_Location), .out_15(Control_Signal_3));  // open: in_2, in_5, out_11, out_14
  MEM_WB_Buffer MEM_WB (
    .Enable(in_1), .Clock(Clock), .Clear(Clear), .PC_IN(PCOUT3), .in_4(Data_Out), .in_5(MEM_Location),
    .in_6(Control_Signal_3), .PC_OUT(MEM_WB_pc_out), .out_13(MEM_WB_out_13), .out_14(MEM_WB_out_14),
    .out_15({MEM_WB_out_15[31:11], WBSelect, MEM_WB_out_15[8:4], WrEN, Control_Signal[2], MEM_WB_out_15[1:0]}));  // open: in_2, in_3, out_11, out_12
  or or_1 (or_1_out, and_2_out, and_3_out);
  Adder #(.width(3)) adder_3 (.a(3'b001), .b(3'b000), .out(adder_3_out));  // open: cin, cout
  Register #(.width(1)) PC_2 (.D(or_1_out), .en(not_1_out), .Q(PC_2_q), .clk(or_1_out), .clr(Stall));
  not not_1 (not_1_out, Stall);
  or or_2 (or_2_out, ~comparator_5_eq, BRANCH_NT);  // OR_Gate
  and and_4 (LdPC, or_2_out, ~Stall);  // AND_Gate
  Register #(.width(3)) PC_3 (.D(adder_3_out), .en(PC_2_q), .Q(PC_3_q), .clk(Clock), .clr(Stall));
  Multiplexer #(.select(2), .width(32), .disabled(0), .enable("false")) multiplexer_6 (
    .in0(MEM_WB_pc_out), .in1(MEM_WB_out_14), .in2(MEM_WB_out_13), .out(Input), .sel(WBSelect));  // open: in3
  Comparator #(.width(3), .mode("unsigned")) comparator_6 (.a(PC_3_q), .b(3'b100), .eq(Stall));  // open: gt, lt

  // Other names for the same wires on the sheet: Destination_Register = Control_Signal[2];
  //   SelectRY = Control_Signal[11]; PC_Address_Sel[1:0] = Control_Signal_2[1:0];
  //   Function[1:0] = Control_Signal_2[5:4]; immediate_Select = Control_Signal_2[6];
  //   Control_Signal_2[7] = Branch_Enable; WrMEM = Control_Signal_3[8]; Enable = in_1;
  //   MEM_Location_In[31:0] = MEM_Location; RX[3:0] = OUT1[23:20]; RY[3:0] = OUT1[27:24]; WrRegNO1[3:0] = OUT1[27:24];
  //   OUT1[31:28] = OPCODE; RZ[3:0] = OUT1[3:0]; Sign_Extended_Immediate[19:0] = OUT1[19:0]

  // Notes on the sheet:
  //   IF/IDRR State
  //   IDRR/EX State
  //   EX/MEM State
  //   MEM/WB State
  //   Control Signals
  //   contents of rom_1 (hex, n*v repeats v):
  //   8 9 c 10c 84 22 48 10
  //   Stall Check
endmodule

module Dual_Ported_Register_File (
  input  CLK,
  input  WrEN,
  input  [3:0] WrREGNO,
  input  [3:0] RdREGNO1,
  input  [3:0] RdREGNO2,
  input  [31:0] INPUT,
  output [31:0] OUT1,
  output [31:0] OUT2
);

  wire En_a0, En_a1, En_a2, En_a3, En_a4, En_at, En_fp, En_k0, En_ra, En_s0, En_s1, En_s2, En_s3, En_sp,
       En_v0;
  wire [31:0] a0, a1, a2, a3, a4, at, fp, k0, ra, s0, s1, s2, s3, sp, v0, zero;

  Decoder #(.select(4), .disabled(0)) decoder_1 (
    .out1(En_at), .out2(En_v0), .out3(En_a0), .out4(En_a1), .out5(En_a2), .out6(En_a3), .out7(En_a4),
    .out8(En_s0), .out9(En_s1), .out10(En_s2), .out11(En_s3), .out12(En_k0), .out13(En_sp), .out14(En_fp),
    .out15(En_ra), .sel(WrREGNO), .en(WrEN));  // open: out0
  Register #(.width(32)) u_zero (.D(INPUT), .en(1'b0), .Q(zero), .clk(CLK));  // open: clr
  Register #(.width(32)) u_at (.D(INPUT), .en(En_at), .Q(at), .clk(CLK));  // open: clr
  Register #(.width(32)) u_v0 (.D(INPUT), .en(En_v0), .Q(v0), .clk(CLK));  // open: clr
  Register #(.width(32)) u_a0 (.D(INPUT), .en(En_a0), .Q(a0), .clk(CLK));  // open: clr
  Register #(.width(32)) u_a1 (.D(INPUT), .en(En_a1), .Q(a1), .clk(CLK));  // open: clr
  Register #(.width(32)) u_a2 (.D(INPUT), .en(En_a2), .Q(a2), .clk(CLK));  // open: clr
  Register #(.width(32)) u_a3 (.D(INPUT), .en(En_a3), .Q(a3), .clk(CLK));  // open: clr
  Register #(.width(32)) u_a4 (.D(INPUT), .en(En_a4), .Q(a4), .clk(CLK));  // open: clr
  Multiplexer #(.select(4), .width(32), .disabled(0), .enable("false")) multiplexer_1 (
    .in0(zero), .in1(at), .in2(v0), .in3(a0), .in4(a1), .in5(a2), .in6(a3), .in7(a4), .in8(s0), .in9(s1),
    .in10(s2), .in11(s3), .in12(k0), .in13(sp), .in14(fp), .in15(ra), .out(OUT2), .sel(RdREGNO2));
  Register #(.width(32)) u_s0 (.D(INPUT), .en(En_s0), .Q(s0), .clk(CLK));  // open: clr
  Register #(.width(32)) u_s1 (.D(INPUT), .en(En_s1), .Q(s1), .clk(CLK));  // open: clr
  Register #(.width(32)) u_s2 (.D(INPUT), .en(En_s2), .Q(s2), .clk(CLK));  // open: clr
  Register #(.width(32)) u_s3 (.D(INPUT), .en(En_s3), .Q(s3), .clk(CLK));  // open: clr
  Register #(.width(32)) u_k0 (.D(INPUT), .en(En_k0), .Q(k0), .clk(CLK));  // open: clr
  Register #(.width(32)) u_sp (.D(INPUT), .en(En_sp), .Q(sp), .clk(CLK));  // open: clr
  Register #(.width(32)) u_fp (.D(INPUT), .en(En_fp), .Q(fp), .clk(CLK));  // open: clr
  Register #(.width(32)) u_ra (.D(INPUT), .en(En_ra), .Q(ra), .clk(CLK));  // open: clr
  Multiplexer #(.select(4), .width(32), .disabled(0), .enable("false")) multiplexer_2 (
    .in0(zero), .in1(at), .in2(v0), .in3(a0), .in4(a1), .in5(a2), .in6(a3), .in7(a4), .in8(s0), .in9(s1),
    .in10(s2), .in11(s3), .in12(k0), .in13(sp), .in14(fp), .in15(ra), .out(OUT1), .sel(RdREGNO1));

  // Notes on the sheet:
  //   MODIFY AT YOUR OWN RISK
endmodule

module IF_IDRR_Buffer (
  input  [31:0] PC_IN,
  input  [31:0] in_2,
  input  [31:0] in_3,
  input  [31:0] in_4,
  input  [31:0] in_5,
  input  [31:0] in_6,
  input  Enable,
  input  Clock,
  input  Clear,
  output [31:0] PC_OUT,
  output [31:0] out_11,
  output [31:0] out_12,
  output [31:0] out_13,
  output [31:0] out_14,
  output [31:0] out_15
);

  Register #(.width(32)) register_1 (.D(PC_IN), .en(Enable), .Q(PC_OUT), .clk(Clock), .clr(Clear));
  Register #(.width(32)) register_2 (.D(in_2), .en(Enable), .Q(out_11), .clk(Clock), .clr(Clear));
  Register #(.width(32)) register_3 (.D(in_3), .en(Enable), .Q(out_12), .clk(Clock), .clr(Clear));
  Register #(.width(32)) register_4 (.D(in_4), .en(Enable), .Q(out_13), .clk(Clock), .clr(Clear));
  Register #(.width(32)) register_5 (.D(in_5), .en(Enable), .Q(out_14), .clk(Clock), .clr(Clear));
  Register #(.width(32)) register_6 (.D(in_6), .en(Enable), .Q(out_15), .clk(Clock), .clr(Clear));
endmodule

module IDRR_EX_Buffer (
  input  [31:0] PC_IN,
  input  [31:0] in_2,
  input  [31:0] in_3,
  input  [31:0] in_4,
  input  [31:0] in_5,
  input  [31:0] in_6,
  input  Enable,
  input  Clock,
  input  Clear,
  output [31:0] PC_OUT,
  output [31:0] out_11,
  output [31:0] out_12,
  output [31:0] out_13,
  output [31:0] out_14,
  output [31:0] out_15
);

  Register #(.width(32)) register_1 (.D(PC_IN), .en(Enable), .Q(PC_OUT), .clk(Clock), .clr(Clear));
  Register #(.width(32)) register_2 (.D(in_2), .en(Enable), .Q(out_11), .clk(Clock), .clr(Clear));
  Register #(.width(32)) register_3 (.D(in_3), .en(Enable), .Q(out_12), .clk(Clock), .clr(Clear));
  Register #(.width(32)) register_4 (.D(in_4), .en(Enable), .Q(out_13), .clk(Clock), .clr(Clear));
  Register #(.width(32)) register_5 (.D(in_5), .en(Enable), .Q(out_14), .clk(Clock), .clr(Clear));
  Register #(.width(32)) register_6 (.D(in_6), .en(Enable), .Q(out_15), .clk(Clock), .clr(Clear));
endmodule

module EX_MEM_Buffer (
  input  [31:0] PC_IN,
  input  [31:0] in_2,
  input  [31:0] in_3,
  input  [31:0] in_4,
  input  [31:0] in_5,
  input  [31:0] in_6,
  input  Enable,
  input  Clock,
  input  Clear,
  output [31:0] PC_OUT,
  output [31:0] out_11,
  output [31:0] out_12,
  output [31:0] out_13,
  output [31:0] out_14,
  output [31:0] out_15
);

  Register #(.width(32)) register_1 (.D(PC_IN), .en(Enable), .Q(PC_OUT), .clk(Clock), .clr(Clear));
  Register #(.width(32)) register_2 (.D(in_2), .en(Enable), .Q(out_11), .clk(Clock), .clr(Clear));
  Register #(.width(32)) register_3 (.D(in_3), .en(Enable), .Q(out_12), .clk(Clock), .clr(Clear));
  Register #(.width(32)) register_4 (.D(in_4), .en(Enable), .Q(out_13), .clk(Clock), .clr(Clear));
  Register #(.width(32)) register_5 (.D(in_5), .en(Enable), .Q(out_14), .clk(Clock), .clr(Clear));
  Register #(.width(32)) register_6 (.D(in_6), .en(Enable), .Q(out_15), .clk(Clock), .clr(Clear));
endmodule

module MEM_WB_Buffer (
  input  [31:0] PC_IN,
  input  [31:0] in_2,
  input  [31:0] in_3,
  input  [31:0] in_4,
  input  [31:0] in_5,
  input  [31:0] in_6,
  input  Enable,
  input  Clock,
  input  Clear,
  output [31:0] PC_OUT,
  output [31:0] out_11,
  output [31:0] out_12,
  output [31:0] out_13,
  output [31:0] out_14,
  output [31:0] out_15
);

  Register #(.width(32)) register_1 (.D(PC_IN), .en(Enable), .Q(PC_OUT), .clk(Clock), .clr(Clear));
  Register #(.width(32)) register_2 (.D(in_2), .en(Enable), .Q(out_11), .clk(Clock), .clr(Clear));
  Register #(.width(32)) register_3 (.D(in_3), .en(Enable), .Q(out_12), .clk(Clock), .clr(Clear));
  Register #(.width(32)) register_4 (.D(in_4), .en(Enable), .Q(out_13), .clk(Clock), .clr(Clear));
  Register #(.width(32)) register_5 (.D(in_5), .en(Enable), .Q(out_14), .clk(Clock), .clr(Clear));
  Register #(.width(32)) register_6 (.D(in_6), .en(Enable), .Q(out_15), .clk(Clock), .clr(Clear));
endmodule

module ALU (
  input  [1:0] FUNC,
  input  [31:0] A,
  input  [31:0] B,
  output [31:0] OUT
);

  wire [31:0] adder_1_out, adder_2_out, nand_1_out, subtractor_1_out;

  Adder #(.width(32)) adder_1 (.a(A), .b(B), .out(adder_1_out), .cin(1'b0));  // open: cout
  assign nand_1_out = ~(A & B);  // NAND_Gate nand_1, 32 bits wide
  Subtractor #(.width(32)) subtractor_1 (.a(A), .b(B), .out(subtractor_1_out), .bin(1'b0));  // open: bout
  Adder #(.width(32)) adder_2 (.a(A), .b({32{1'b0}}), .out(adder_2_out), .cin(1'b1));  // open: cout
  Multiplexer #(.select(2), .width(32), .disabled(0), .enable("false")) multiplexer_1 (
    .in0(adder_1_out), .in1(nand_1_out), .in2(subtractor_1_out), .in3(adder_2_out), .out(OUT), .sel(FUNC));

  // Notes on the sheet:
  //   MODIFY AT YOUR OWN RISK
endmodule
