// Logisim project LC-2200-16.circ as structural Verilog: 7 circuits, main circuit 1 - bit Adder
module LC_2200 (
  input  RegSelLo,
  input  Clear,
  input  RegSelHi,
  input  ALULo,
  input  ALUHi,
  input  DrPC,
  input  LdPC,
  input  LdA,
  input  LdB,
  input  DrALU,
  input  DrREG,
  input  WrREG,
  input  DrMEM,
  input  WrMEM,
  input  LdMAR,
  input  LdIR,
  input  DrOFF,
  input  LdZ,
  output [15:0] Bus_Value,
  output [15:0] Dout,
  output [3:0] RegNo,
  output Z,
  output [2:0] OPCODE
);

  wire _0, _1, _2, _3, _4, _5, _6, _7, _8, _9, _10, _11, _12, Clock, nor_1_out;
  wire [15:0] A_q, B_q, bit_extender_1_out, MAR_q, n16_bit_alu_1_s, PC_q, ram_1_data;

  Clock u_Clock (.out(Clock));
  Register #(.width(16)) PC (.D(Bus_Value), .en(LdPC), .Q(PC_q), .clk(Clock), .clr(Clear));
  assign Bus_Value = DrPC ? PC_q : 16'bz;  // Controlled_Buffer DrPC
  Register #(.width(16)) A (.D(Bus_Value), .en(LdA), .Q(A_q), .clk(Clock), .clr(Clear));
  _16___bit_ALU u_16_bit_alu_1 (.A(A_q), .B(B_q), .Function({ALUHi, ALULo}), .S(n16_bit_alu_1_s));  // open: Cin
  assign Bus_Value = DrALU ? n16_bit_alu_1_s : 16'bz;  // Controlled_Buffer controlled_buffer_1
  Register #(.width(16)) B (.D(Bus_Value), .en(LdB), .Q(B_q), .clk(Clock), .clr(Clear));
  Registers registers_1 (.RegNo(RegNo), .Data(Bus_Value), .WrREG(WrREG), .S(Dout));
  assign Bus_Value = DrREG ? Dout : 16'bz;  // Controlled_Buffer controlled_buffer_2
  Multiplexer #(.select(2), .width(4), .enable("false")) multiplexer_1 (
    .in0({_12, _11, _10, _9}), .in1({_8, _7, _6, _5}), .in2({_0, _1, _2, _3}), .out(RegNo),
    .sel({RegSelHi, RegSelLo}));  // open: in3
  Register #(.width(16)) MAR (.D(Bus_Value), .en(LdMAR), .Q(MAR_q), .clk(Clock), .clr(Clear));
  RAM #(.addrWidth(16), .dataWidth(16), .bus("separate")) ram_1 (
    .addr(MAR_q), .din(Bus_Value), .data(ram_1_data), .str(WrMEM), .clk(Clock), .ld(1'b1), .clr(Clear));  // open: sel
  assign Bus_Value = DrMEM ? ram_1_data : 16'bz;  // Controlled_Buffer controlled_buffer_3
  Register #(.width(16)) IR (
    .D(Bus_Value), .en(LdIR), .Q({OPCODE, _12, _11, _10, _9, _8, _7, _6, _5, _4, _3, _2, _1, _0}),
    .clk(Clock), .clr(Clear));
  assign bit_extender_1_out = {{11{_4}}, {_4, _3, _2, _1, _0}};  // Bit_Extender bit_extender_1
  assign Bus_Value = DrOFF ? bit_extender_1_out : 16'bz;  // Controlled_Buffer controlled_buffer_4
  nor nor_1 (nor_1_out, Bus_Value[0], Bus_Value[1], Bus_Value[2], Bus_Value[3], Bus_Value[4], Bus_Value[5], Bus_Value[6], Bus_Value[7], Bus_Value[8], Bus_Value[9], Bus_Value[10], Bus_Value[11], Bus_Value[12], Bus_Value[13], Bus_Value[14], Bus_Value[15]);
  Register #(.width(1)) register_1 (.D(nor_1_out), .en(LdZ), .Q(Z), .clk(Clock), .clr(Clear));

  // Other names for the same wires on the sheet: Func[1:0] = {ALUHi, ALULo};
  //   IR[15:0] = {OPCODE, _12, _11, _10, _9, _8, _7, _6, _5, _4, _3, _2, _1, _0}; offset[4:0] = {_4, _3, _2, _1, _0};
  //   _13 = OPCODE[0]; _14 = OPCODE[1]; _15 = OPCODE[2]; RegSel[1:0] = {RegSelHi, RegSelLo};
  //   RX[3:0] = {_12, _11, _10, _9}; RY[3:0] = {_8, _7, _6, _5}; RZ[3:0] = {_0, _1, _2, _3}

  // Notes on the sheet:
  //   Mani Japra (902958199)
  //   SPRING 2016
endmodule

module microcontroller (
  input  Clear,
  output [2:0] OPCODE
);

  wire clock_1_out;
  wire [0:0] lc_2200_1_z;
  wire [5:0] multiplexer_1_out, Next, register_1_q, rom_2_data, rom_3_data;
  wire [24:6] rom_1_data;

  ROM #(.addrWidth(6), .dataWidth(25)) rom_1 (.addr(register_1_q), .data({rom_1_data, Next}));  // open: sel
  Register #(.width(6)) register_1 (.D(multiplexer_1_out), .Q(register_1_q), .clk(clock_1_out));  // open: en, clr
  Clock clock_1 (.out(clock_1_out));
  LC_2200 lc_2200_1 (
    .RegSelLo(rom_1_data[19]), .Clear(Clear), .RegSelHi(rom_1_data[20]), .ALULo(rom_1_data[21]),
    .ALUHi(rom_1_data[22]), .DrPC(rom_1_data[9]), .LdPC(rom_1_data[11]), .LdA(rom_1_data[14]),
    .LdB(rom_1_data[15]), .DrALU(rom_1_data[8]), .DrREG(rom_1_data[6]), .WrREG(rom_1_data[17]),
    .DrMEM(rom_1_data[7]), .WrMEM(rom_1_data[18]), .LdMAR(rom_1_data[13]), .LdIR(rom_1_data[12]),
    .DrOFF(rom_1_data[10]), .LdZ(rom_1_data[16]), .Z(lc_2200_1_z[0]), .OPCODE(OPCODE));  // open: Bus_Value, Dout, RegNo
  Multiplexer #(.select(2), .width(6), .enable("false")) multiplexer_1 (
    .in0(Next), .in1(rom_3_data), .in2(rom_2_data), .out(multiplexer_1_out), .sel(rom_1_data[24:23]));  // open: in3
  ROM #(.addrWidth(2), .dataWidth(6)) rom_2 (.addr({1'b0, lc_2200_1_z[0]}), .data(rom_2_data));  // open: sel
  ROM #(.addrWidth(3), .dataWidth(6)) rom_3 (.addr(OPCODE), .data(rom_3_data));  // open: sel

  // Notes on the sheet:
  //   contents of rom_1 (hex, n*v repeats v):
  //   6201 1082 e00900 84044 108045 20100 88047 4408 420100 8404a 840b 20100 8404d 840e 210f 20080 84051
  //   8412 2113 40040 4055 88056 1410100 4218 8419 900 a021b 840 1c 8805e 441f 420100
  //   Z ROM
  //   contents of rom_2 (hex, n*v repeats v):
  //   0 17
  //   Sequencer ROM
  //   contents of rom_3 (hex, n*v repeats v):
  //   3 6 9 c 10 14 1a 1c
endmodule

module _1___bit_Adder (
  input  A,
  input  B,
  input  Cin,
  output S,
  output Cout
);

  wire A___B_out, A___Cin_out, B___Cin_out, or_1_out, xor_1_out;

  and A___B (A___B_out, A, B);
  and B___Cin (B___Cin_out, B, Cin);
  and A___Cin (A___Cin_out, A, Cin);
  xor xor_1 (xor_1_out, A, B);
  or or_1 (or_1_out, A___B_out, B___Cin_out);
  xor xor_2 (S, xor_1_out, Cin);
  or or_2 (Cout, or_1_out, A___Cin_out);
endmodule

module _4___bit_Adder (
  input  [3:0] A,
  input  [3:0] B,
  input  Cin,
  output [3:0] S,
  output Cout
);

  wire n1_bit_adder_1_cout, n1_bit_adder_2_cout, n1_bit_adder_3_cout;

  _1___bit_Adder u_1_bit_adder_1 (.A(A[0]), .B(B[0]), .Cin(Cin), .S(S[0]), .Cout(n1_bit_adder_1_cout));
  _1___bit_Adder u_1_bit_adder_2 (.A(A[1]), .B(B[1]), .Cin(n1_bit_adder_1_cout), .S(S[1]), .Cout(n1_bit_adder_2_cout));
  _1___bit_Adder u_1_bit_adder_3 (.A(A[2]), .B(B[2]), .Cin(n1_bit_adder_2_cout), .S(S[2]), .Cout(n1_bit_adder_3_cout));
  _1___bit_Adder u_1_bit_adder_4 (.A(A[3]), .B(B[3]), .Cin(n1_bit_adder_3_cout), .S(S[3]), .Cout(Cout));

  // Other names for the same wires on the sheet: Out0 = S[0]; Out1 = S[1]; Out2 = S[2]; Out3 = S[3]
endmodule

module _16___bit_Adder (
  input  [15:0] A,
  input  [15:0] B,
  input  Cin,
  output out_4,
  output [15:0] S
);

  wire n4_bit_adder_1_cout, n4_bit_adder_2_cout, n4_bit_adder_3_cout;

  _4___bit_Adder u_4_bit_adder_1 (.Cin(Cin), .A(A[3:0]), .B(B[3:0]), .S(S[3:0]), .Cout(n4_bit_adder_1_cout));
  _4___bit_Adder u_4_bit_adder_2 (
    .Cin(n4_bit_adder_1_cout), .A(A[7:4]), .B(B[7:4]), .S(S[7:4]), .Cout(n4_bit_adder_2_cout));
  _4___bit_Adder u_4_bit_adder_3 (
    .Cin(n4_bit_adder_2_cout), .A(A[11:8]), .B(B[11:8]), .S(S[11:8]), .Cout(n4_bit_adder_3_cout));
  _4___bit_Adder u_4_bit_adder_4 (.Cin(n4_bit_adder_3_cout), .A(A[15:12]), .B(B[15:12]), .S(S[15:12]), .Cout(out_4));

  // Other names for the same wires on the sheet: A0[3:0] = A[3:0]; A1[3:0] = A[7:4]; A2[3:0] = A[11:8];
  //   A3[3:0] = A[15:12]; B0[3:0] = B[3:0]; B1[3:0] = B[7:4]; B2[3:0] = B[11:8]; B3[3:0] = B[15:12]; Cout = out_4;
  //   Out0[3:0] = S[3:0]; Out1[3:0] = S[7:4]; Out2[3:0] = S[11:8]; Out3[3:0] = S[15:12]
endmodule

module _16___bit_ALU (
  input  [15:0] A,
  input  [15:0] B,
  input  Cin,
  input  [1:0] Function,
  output [15:0] S
);

  wire Cout;
  wire [15:0] A___1, A___B, A___B_t, NAND;

  Multiplexer #(.select(2), .width(16), .enable("false")) multiplexer_1 (
    .in0(A___B), .in1(NAND), .in2(A___B_t), .in3(A___1), .out(S), .sel(Function));
  Adder #(.width(16)) adder_1 (.a(A), .b(B), .out(A___B), .cin(Cin), .cout(Cout));
  assign NAND = ~(A & B);  // NAND_Gate nand_1, 16 bits wide
  Subtractor #(.width(16)) subtractor_1 (.a(A), .b(B), .out(A___B_t), .bin(Cin), .bout(Cout));
  Adder #(.width(16)) adder_2 (.a(A), .b(16'h1), .out(A___1), .cin(Cin), .cout(Cout));

  // Other names for the same wires on the sheet: F[1:0] = Function
endmodule

module Registers (
  input  [3:0] RegNo,
  input  [15:0] Data,
  input  WrREG,
  output [15:0] S
);

  wire Wr0, Wr1, Wr2, Wr3, Wr4, Wr5, Wr6, Wr7, Wr8, Wr9, Wr10, Wr11, Wr12, Wr13, Wr14, Wr15, WrReg0, WrReg1,
       WrReg2, WrReg3, WrReg4, WrReg5, WrReg6, WrReg7, WrReg8, WrReg9, WrReg10, WrReg11, WrReg12, WrReg13,
       WrReg14, WrReg15;
  wire [15:0] _0, _1, _2, _3, _4, _5, _6, _7, _8, _9, _10, _11, _12, _13, _14, _15, S0, S1, S2, S3, S4, S5,
       S6, S7, S8, S9, S10, S11, S12, S13, S14, S15;

  Register #(.width(16)) zero (.D(_0), .Q(S0), .clk(WrReg0));  // open: en, clr
  Register #(.width(16)) at (.D(_1), .Q(S1), .clk(WrReg1));  // open: en, clr
  Register #(.width(16)) v0 (.D(_2), .Q(S2), .clk(WrReg2));  // open: en, clr
  Register #(.width(16)) a0 (.D(_3), .Q(S3), .clk(WrReg3));  // open: en, clr
  Demultiplexer #(.select(4), .width(16), .enable("false")) demultiplexer_1 (
    .out0(_0), .out1(_1), .out2(_2), .out3(_3), .out4(_4), .out5(_5), .out6(_6), .out7(_7), .out8(_8),
    .out9(_9), .out10(_10), .out11(_11), .out12(_12), .out13(_13), .out14(_14), .out15(_15), .in(Data),
    .sel(RegNo));
  Multiplexer #(.select(4), .width(16), .enable("false")) multiplexer_1 (
    .in0(S0), .in1(S1), .in2(S2), .in3(S3), .in4(S4), .in5(S5), .in6(S6), .in7(S7), .in8(S8), .in9(S9),
    .in10(S10), .in11(S11), .in12(S12), .in13(S13), .in14(S14), .in15(S15), .out(S), .sel(RegNo));
  Register #(.width(16)) a1 (.D(_4), .Q(S4), .clk(WrReg4));  // open: en, clr
  Register #(.width(16)) a2 (.D(_5), .Q(S5), .clk(WrReg5));  // open: en, clr
  Register #(.width(16)) t0 (.D(_6), .Q(S6), .clk(WrReg6));  // open: en, clr
  Register #(.width(16)) t1 (.D(_7), .Q(S7), .clk(WrReg7));  // open: en, clr
  Register #(.width(16)) t2 (.D(_8), .Q(S8), .clk(WrReg8));  // open: en, clr
  Register #(.width(16)) u_s0 (.D(_9), .Q(S9), .clk(WrReg9));  // open: en, clr
  Register #(.width(16)) u_s1 (.D(_10), .Q(S10), .clk(WrReg10));  // open: en, clr
  Register #(.width(16)) u_s2 (.D(_11), .Q(S11), .clk(WrReg11));  // open: en, clr
  Register #(.width(16)) k0 (.D(_12), .Q(S12), .clk(WrReg12));  // open: en, clr
  Register #(.width(16)) sp (.D(_13), .Q(S13), .clk(WrReg13));  // open: en, clr
  Register #(.width(16)) fp (.D(_14), .Q(S14), .clk(WrReg14));  // open: en, clr
  Register #(.width(16)) ra (.D(_15), .Q(S15), .clk(WrReg15));  // open: en, clr
  Decoder #(.select(4), .enable("false")) decoder_1 (
    .out0(Wr0), .out1(Wr1), .out2(Wr2), .out3(Wr3), .out4(Wr4), .out5(Wr5), .out6(Wr6), .out7(Wr7),
    .out8(Wr8), .out9(Wr9), .out10(Wr10), .out11(Wr11), .out12(Wr12), .out13(Wr13), .out14(Wr14),
    .out15(Wr15), .sel(RegNo));
  and and_1 (WrReg0, Wr0, WrREG);
  and and_2 (WrReg1, Wr1, WrREG);
  and and_3 (WrReg2, Wr2, WrREG);
  and and_4 (WrReg3, Wr3, WrREG);
  and and_5 (WrReg4, Wr4, WrREG);
  and and_6 (WrReg5, Wr5, WrREG);
  and and_7 (WrReg6, Wr6, WrREG);
  and and_8 (WrReg7, Wr7, WrREG);
  and and_9 (WrReg8, Wr8, WrREG);
  and and_10 (WrReg9, Wr9, WrREG);
  and and_11 (WrReg10, Wr10, WrREG);
  and and_12 (WrReg11, Wr11, WrREG);
  and and_13 (WrReg12, Wr12, WrREG);
  and and_14 (WrReg13, Wr13, WrREG);
  and and_15 (WrReg14, Wr14, WrREG);
  and and_16 (WrReg15, Wr15, WrREG);
endmodule
